# Fritzing sketch laserx-shoot-back (saved by Fritzing 0.9.6b)
breadboards: 1

parts:
  Part1 = Arduino Leonardo (Rev3b)
  IR1 = vs1838b [package=THT]
  Mod1 = KY-016 RGB Full Color LED Module [package="Breakout board"]
  D1 = LTE-302 [package=lte-302]
  R1 = Resistor [tolerance=±5% resistance=220 package="0805 [SMD]"]

nets:
  N1: Part1.D2/SDA, IR1.Data
  N2: Part1.D3_PWM/SCL, R1.Pin_0
  N3: Part1.5V, IR1.Vs
  GND: Part1.GND, IR1.GND, Mod1.-, D1.C
  N4: Part1.D9_PWM/A9, Mod1.B
  N5: Part1.D10_PWM/A10, Mod1.G
  N6: Part1.D11_PWM, Mod1.R
  N7: D1.A, R1.Pin_1

custom parts:
  KY-016 RGB Full Color LED Module: KY-016 Arduino full color 5mm RGB LED, different colors can be obtained by mixing the three primary colors.
